// Logisim project Dec.circ as structural Verilog
module main (
  input  w,
  input  x,
  input  y,
  input  z,
  output f_w_x_y_z
);

  wire dec_4x16_a8c844dc_1_out_5, dec_4x16_a8c844dc_1_out_6, dec_4x16_a8c844dc_1_out_7,
       dec_4x16_a8c844dc_1_out_8, dec_4x16_a8c844dc_1_out_9, dec_4x16_a8c844dc_1_out_10,
       dec_4x16_a8c844dc_1_out_11, dec_4x16_a8c844dc_1_out_12, dec_4x16_a8c844dc_1_out_13,
       dec_4x16_a8c844dc_1_out_14, dec_4x16_a8c844dc_1_out_15, dec_4x16_a8c844dc_1_out_16,
       dec_4x16_a8c844dc_1_out_17, dec_4x16_a8c844dc_1_out_18, dec_4x16_a8c844dc_1_out_19,
       dec_4x16_a8c844dc_1_out_20;

  Dec_4x16_a8c844dc dec_4x16_a8c844dc_1 (
    .B(x), .C(y), .D(z), .A(w), .out_20(dec_4x16_a8c844dc_1_out_20), .out_5(dec_4x16_a8c844dc_1_out_5),
    .out_6(dec_4x16_a8c844dc_1_out_6), .out_7(dec_4x16_a8c844dc_1_out_7), .out_8(dec_4x16_a8c844dc_1_out_8),
    .out_9(dec_4x16_a8c844dc_1_out_9), .out_10(dec_4x16_a8c844dc_1_out_10),
    .out_11(dec_4x16_a8c844dc_1_out_11), .out_12(dec_4x16_a8c844dc_1_out_12),
    .out_13(dec_4x16_a8c844dc_1_out_13), .out_14(dec_4x16_a8c844dc_1_out_14),
    .out_15(dec_4x16_a8c844dc_1_out_15), .out_16(dec_4x16_a8c844dc_1_out_16),
    .out_17(dec_4x16_a8c844dc_1_out_17), .out_18(dec_4x16_a8c844dc_1_out_18),
    .out_19(dec_4x16_a8c844dc_1_out_19));
  or or_1 (f_w_x_y_z, dec_4x16_a8c844dc_1_out_5, dec_4x16_a8c844dc_1_out_6, dec_4x16_a8c844dc_1_out_9, dec_4x16_a8c844dc_1_out_10, dec_4x16_a8c844dc_1_out_11);
endmodule

module Dec_4x16_a8c844dc (
  input  A,
  input  B,
  input  C,
  input  D,
  output out_5,
  output out_6,
  output out_7,
  output out_8,
  output out_9,
  output out_10,
  output out_11,
  output out_12,
  output out_13,
  output out_14,
  output out_15,
  output out_16,
  output out_17,
  output out_18,
  output out_19,
  output out_20
);

  and and_1 (out_5, ~A, ~B, ~C, ~D);  // AND_Gate
  and and_2 (out_6, ~A, ~B, ~C, D);  // AND_Gate
  and and_3 (out_7, ~A, ~B, C, ~D);  // AND_Gate
  and and_4 (out_8, ~A, ~B, C, D);  // AND_Gate
  and and_5 (out_9, ~A, B, ~C, ~D);  // AND_Gate
  and and_6 (out_10, ~A, B, ~C, D);  // AND_Gate
  and and_7 (out_11, ~A, B, C, ~D);  // AND_Gate
  and and_8 (out_12, ~A, B, C, D);  // AND_Gate
  and and_9 (out_13, A, ~B, ~C, ~D);  // AND_Gate
  and and_10 (out_14, A, ~B, ~C, D);  // AND_Gate
  and and_11 (out_15, A, ~B, C, ~D);  // AND_Gate
  and and_12 (out_16, A, ~B, C, D);  // AND_Gate
  and and_13 (out_17, A, B, ~C, ~D);  // AND_Gate
  and and_14 (out_18, A, B, ~C, D);  // AND_Gate
  and and_15 (out_19, A, B, C, ~D);  // AND_Gate
  and and_16 (out_20, A, B, C, D);
endmodule

// VHDL entity Dec4x16, as the project stores it:
-- Universidade de Brasília (UnB)
-- Laboratório de Sistemas Digitais - Turma 07
-- Autor: Henrique Morcelles Salum
-- Data: //2024
-- Relatório 3 - Questão 2

-- **********************************************
-- Circuito: decodificador 4x16:
--             A: vetor de entrada
--             Y: vetor de saída
-- **********************************************

library IEEE;
use IEEE.std_logic_1164.all;

entity Dec4x16 is
    port (
        A: in std_logic_vector(3 downto 0);
        Y: out std_logic_vector(15 downto 0)
    );
end entity Dec4x16;

architecture behavioral of Dec4x16 is
begin
    with A select Y <=
        X"0001" when X"0",
        X"0002" when X"1",
        X"0004" when X"2",
        X"0008" when X"3",
        X"0010" when X"4",
        X"0020" when X"5",
        X"0040" when X"6",
        X"0080" when X"7",
        X"0100" when X"8",
        X"0200" when X"9",
        X"0400" when X"A",
        X"0800" when X"B",
        X"1000" when X"C",
        X"2000" when X"D",
        X"4000" when X"E",
        X"8000" when X"F",
        "----------------" when others;
end architecture behavioral;
