// Logisim project Mux.circ as structural Verilog: 4 circuits, main circuit main
module main (
  input  RST,
  input  [3:0] D,
  input  L,
  input  R,
  output [3:0] Q
);

  wire CLK, mux4x1_1_y, mux4x1_2_y, mux4x1_3_y, mux4x1_4_y;
  wire [1:0] S;

  Clock clock_1 (.out(CLK));
  Mux4x1 mux4x1_1 (.\D₀ (Q[3]), .\D₁ (R), .\D₂ (Q[2]), .\D₃ (D[3]), .S(S), .Y(mux4x1_1_y));
  Mux4x1 mux4x1_2 (.\D₀ (Q[2]), .\D₁ (Q[3]), .\D₂ (Q[1]), .\D₃ (D[2]), .S(S), .Y(mux4x1_2_y));
  Mux4x1 mux4x1_3 (.\D₀ (Q[1]), .\D₁ (Q[2]), .\D₂ (Q[0]), .\D₃ (D[1]), .S(S), .Y(mux4x1_3_y));
  Mux4x1 mux4x1_4 (.\D₀ (Q[0]), .\D₁ (Q[1]), .\D₂ (L), .\D₃ (D[0]), .S(S), .Y(mux4x1_4_y));
  FlipFlopJK flipflopjk_1 (.CLK(CLK), .J(mux4x1_1_y), .K(mux4x1_1_y), .PR(1'b0), .CLR(RST), .Q(Q[3]));
  FlipFlopJK flipflopjk_2 (.CLK(CLK), .J(mux4x1_2_y), .K(mux4x1_2_y), .PR(1'b0), .CLR(RST), .Q(Q[2]));
  FlipFlopJK flipflopjk_3 (.CLK(CLK), .J(mux4x1_3_y), .K(mux4x1_3_y), .PR(1'b0), .CLR(RST), .Q(Q[1]));
  FlipFlopJK flipflopjk_4 (.CLK(CLK), .J(mux4x1_4_y), .K(mux4x1_4_y), .PR(1'b0), .CLR(RST), .Q(Q[0]));
endmodule

module Mux4x1 (
  input  [1:0] S,
  input  \D₀ ,
  input  \D₁ ,
  input  \D₂ ,
  input  \D₃ ,
  output Y
);

  wire and_1_out, and_2_out, and_3_out, and_4_out;

  and and_1 (and_1_out, \D₀ , ~S[1], ~S[0]);  // AND_Gate
  and and_2 (and_2_out, \D₁ , ~S[1], S[0]);  // AND_Gate
  and and_3 (and_3_out, \D₂ , S[1], ~S[0]);  // AND_Gate
  and and_4 (and_4_out, \D₃ , S[1], S[0]);
  or or_1 (Y, and_1_out, and_2_out, and_3_out, and_4_out);
endmodule

module Mux8x1 (
  input  S_36fa348e,
  input  S_0e805c6e,
  input  S_de45d96e,
  input  D_d2348313,
  input  D_d72e01c3,
  input  D_c6ac26ca,
  input  D_45745a7c,
  input  D_7ba976b1,
  input  D_75a2c752,
  input  D_8d387635,
  input  D_a17283b4,
  output Y
);

  wire and_1_out, and_2_out, and_3_out, and_4_out, and_5_out, and_6_out, and_7_out, and_8_out;

  and and_1 (and_1_out, D_d2348313, ~S_36fa348e, ~S_0e805c6e, ~S_de45d96e);  // AND_Gate
  and and_2 (and_2_out, D_d72e01c3, ~S_36fa348e, ~S_0e805c6e, S_de45d96e);  // AND_Gate
  and and_3 (and_3_out, D_c6ac26ca, ~S_36fa348e, S_0e805c6e, ~S_de45d96e);  // AND_Gate
  and and_4 (and_4_out, D_45745a7c, ~S_36fa348e, S_0e805c6e, S_de45d96e);  // AND_Gate
  and and_5 (and_5_out, D_7ba976b1, S_36fa348e, ~S_0e805c6e, ~S_de45d96e);  // AND_Gate
  and and_6 (and_6_out, D_75a2c752, S_36fa348e, ~S_0e805c6e, S_de45d96e);  // AND_Gate
  and and_7 (and_7_out, D_8d387635, S_36fa348e, S_0e805c6e, ~S_de45d96e);  // AND_Gate
  and and_8 (and_8_out, D_a17283b4, S_36fa348e, S_0e805c6e, S_de45d96e);
  or or_1 (Y, and_1_out, and_2_out, and_3_out, and_4_out, and_5_out, and_6_out, and_7_out, and_8_out);
endmodule

module FlipFlopJK (
  input  PR,
  input  J,
  input  K,
  input  CLK,
  input  CLR,
  output Q
);

  wire not_1_out;

  J_K_Flip_Flop j_k_ff_1 (.J(J), .K(not_1_out), .clk(CLK), .Q(Q), .preset(PR), .reset(CLR));  // open: Qn
  not not_1 (not_1_out, K);
endmodule
