// Logisim project Somadores.circ as structural Verilog: 3 circuits, main circuit main
module main (
);

  wire half_adder_1_cout, half_adder_1_s, undriven, undriven_2;

  Half_Adder half_adder_1 (.B(undriven_2), .A(undriven), .Cout(half_adder_1_cout), .S(half_adder_1_s));
endmodule

module Half_Adder (
  input  A,
  input  B,
  output S,
  output Cout
);

  xor xor_1 (S, A, B);
  and and_1 (Cout, A, B);
endmodule

module Full_Adder (
  input  A,
  input  B,
  input  in,
  output S,
  output C
);

  wire and_1_out, and_2_out, and_3_out;

  and and_1 (and_1_out, A, B);
  and and_2 (and_2_out, A, in);
  and and_3 (and_3_out, B, in);
  ExactlyOne xor_1 (.out(S), .in0(A), .in1(B), .in2(in));
  or or_1 (C, and_1_out, and_2_out, and_3_out);

  // Notes on the sheet:
  //   C
  //   out
endmodule
