// Logisim project Questao_1b.circ as structural Verilog: 1 circuit, main circuit main
module main (
  input  A,
  input  B,
  output Z
);

  nand nand_1 (Z, ~A, ~B);  // NAND_Gate
endmodule
