// Logisim project Questao_2a.circ as structural Verilog: 1 circuit, main circuit main
module main (
  input  A,
  input  B,
  input  C,
  output T
);

  wire and_1_out, and_2_out, and_3_out;

  and and_1 (and_1_out, A, B);
  and and_2 (and_2_out, A, C);
  or or_1 (T, and_1_out, and_2_out, and_3_out);
  and and_3 (and_3_out, B, C);
endmodule
