// Logisim project Questao_3b2.circ as structural Verilog: 1 circuit, main circuit main
module main (
  input  A,
  input  B,
  input  C,
  output S
);

  wire nand_1_out, nand_2_out, nand_3_out, nand_4_out;

  nand nand_1 (nand_1_out, ~A, ~B, C);  // NAND_Gate
  nand nand_2 (nand_2_out, ~A, B, ~C);  // NAND_Gate
  nand nand_3 (nand_3_out, A, ~B, ~C);  // NAND_Gate
  nand nand_4 (nand_4_out, A, B, C);
  nand nand_5 (S, nand_1_out, nand_2_out, nand_3_out, nand_4_out);
endmodule
