// Logisim project Questao_4.circ as structural Verilog: 1 circuit, main circuit main
module main (
  input  \D₀ ,
  input  \D₁ ,
  input  \D₂ ,
  input  \D₃ ,
  input  \S₁ ,
  input  \S₀ ,
  output Y
);

  wire nand_1_out, nand_2_out, nand_3_out, nand_4_out, nand_5_out, nand_6_out;

  nand nand_1 (nand_1_out, \S₁ , \S₁ );
  nand nand_2 (nand_2_out, \S₀ , \S₀ );
  nand nand_3 (nand_3_out, \D₀ , nand_1_out, nand_2_out);
  nand nand_4 (nand_4_out, \D₁ , nand_1_out, \S₀ );
  nand nand_5 (nand_5_out, \D₂ , \S₁ , nand_2_out);
  nand nand_6 (nand_6_out, \D₃ , \S₁ , \S₀ );
  nand nand_7 (Y, nand_3_out, nand_4_out, nand_5_out, nand_6_out);
endmodule
