// Logisim project Questao_4_2.circ as structural Verilog: 1 circuit, main circuit main
module main (
  input  \D₀ ,
  input  \D₁ ,
  input  \D₂ ,
  input  \D₃ ,
  input  \S₁ ,
  input  \S₀ ,
  output Y
);

  wire nand_1_out, nand_2_out, nand_3_out, nand_4_out;

  nand nand_1 (nand_1_out, \D₀ , ~\S₁ , ~\S₀ );  // NAND_Gate
  nand nand_2 (nand_2_out, \D₁ , ~\S₁ , \S₀ );  // NAND_Gate
  nand nand_3 (nand_3_out, \D₂ , \S₁ , ~\S₀ );  // NAND_Gate
  nand nand_4 (nand_4_out, \D₃ , \S₁ , \S₀ );
  nand nand_5 (Y, nand_1_out, nand_2_out, nand_3_out, nand_4_out);
endmodule
